# Fritzing sketch christmas_tunes (saved by Fritzing 0.7.10b)
breadboards: 1

parts:
  Arduino1 = Arduino
  R1 = Resistor [tolerance=±5% resistance=220 package=THT]
  S1 = Pushbutton [package=THT]
  J1 = Piezo Speaker
  LED1 = LED - 5mm [color="Red (633nm)" package="5 mm [THT]"]
  LED2 = LED - 5mm [color="Red (633nm)" package="5 mm [THT]"]
  LED3 = LED - 5mm [color="Red (633nm)" package="5 mm [THT]"]
  LED4 = LED - 5mm [color="Red (633nm)" package="5 mm [THT]"]
  LED5 = LED - 5mm [color="Red (633nm)" package="5 mm [THT]"]

nets:
  N1: Arduino1.GND, R1.Pin_1, J1.pin2, LED1.cathode, LED2.cathode, LED3.cathode, LED4.cathode, LED5.cathode
  N2: Arduino1.D8, J1.pin1
  N3: Arduino1.D7, LED5.anode
  N4: Arduino1.D6, LED4.anode
  N5: Arduino1.D5, LED3.anode
  N6: Arduino1.D4, LED2.anode
  N7: Arduino1.D3, LED1.anode
  N8: Arduino1.D2, R1.Pin_0
  N9: Arduino1.+5V, S1.leg1
